// Logisim project Lab3_Procesador_Monociclo.circ as structural Verilog: 11 circuits, main circuit main
module main (
);

  wire alu_1_zero, ALUSrc, and_1_out, Branch, CLK, Jump, JumpReg, Link, MemRead, MemToRead, MemWrite, RegDst,
       RegWrite, Reset;
  wire [1:0] ALUOp;
  wire [2:0] alucontrol_1_aluopout;
  wire [4:0] multiplexer_1_out, multiplexer_2_out, rd, rs, rt, shamt;
  wire [5:0] funct, opcode;
  wire [15:0] immediate;
  wire [25:0] Address;
  wire [31:0] adder_1_out, alu_1_aluresult, datamem_1_readdata, extend16_1_out_2, ifetch_1_instruction,
       multiplexer_3_out, multiplexer_4_out, multiplexer_6_out, multiplexer_7_out, NextPC, PCPlus4,
       ReadData1, shifter_1_out, splitjumpaddress_1_addressjump, WriteData, WriteMData;

  Button button_1 (.out(Reset));
  Clock clock_1 (.out(CLK));
  IFetch ifetch_1 (.nextPC(NextPC), .CLK(CLK), .Reset(Reset), .PCplus4(PCPlus4), .Instruction(ifetch_1_instruction));
  // Probe on opcode
  ISplit isplit_1 (
    .Instruction(ifetch_1_instruction), .opcode(opcode), .immediate(immediate), .address(Address),
    .funct(funct), .shamt(shamt), .rd(rd), .rt(rt), .rs(rs));
  Control control_1 (
    .OpCode(opcode), .RegDst(RegDst), .Jump(Jump), .Branch(Branch), .MemRead(MemRead), .MemToReg(MemToRead),
    .ALUOp(ALUOp), .MemWrite(MemWrite), .ALUSrc(ALUSrc), .RegWrite(RegWrite), .Link(Link));
  Multiplexer #(.width(5)) multiplexer_1 (.in0(rt), .in1(rd), .out(multiplexer_1_out), .sel(RegDst));
  Multiplexer #(.width(5)) multiplexer_2 (
    .in0(multiplexer_1_out), .in1({5{1'b1}}), .out(multiplexer_2_out), .sel(Link));
  Extend16 extend16_1 (.in_1(immediate), .out_2(extend16_1_out_2));
  RegFile regfile_1 (
    .ReadReg1(rs), .ReadReg2(rt), .WriteRegister(multiplexer_2_out), .WriteData(WriteData), .CLK(CLK),
    .RegWrite(RegWrite), .Reset(Reset), .out_9(WriteMData), .ReadData1(ReadData1));
  Shifter #(.width(32)) shifter_1 (.in(extend16_1_out_2), .\dist (5'b00010), .out(shifter_1_out));
  ALUControl alucontrol_1 (.ALUOpIn(ALUOp), .Instruction(funct), .ALUOpOut(alucontrol_1_aluopout), .JumpReg(JumpReg));
  Adder #(.width(32)) adder_1 (.a(PCPlus4), .b(shifter_1_out), .out(adder_1_out));  // open: cin, cout
  Multiplexer #(.width(32)) multiplexer_3 (
    .in0(WriteMData), .in1(extend16_1_out_2), .out(multiplexer_3_out), .sel(ALUSrc));
  and and_1 (and_1_out, Branch, alu_1_zero);
  ALU alu_1 (
    .ALUOperation(alucontrol_1_aluopout), .A(ReadData1), .B(multiplexer_3_out), .ALUResult(alu_1_aluresult),
    .zero(alu_1_zero));
  Multiplexer #(.width(32)) multiplexer_4 (.in0(PCPlus4), .in1(adder_1_out), .out(multiplexer_4_out), .sel(and_1_out));
  Multiplexer #(.width(32)) multiplexer_5 (.in0(multiplexer_6_out), .in1(ReadData1), .out(NextPC), .sel(JumpReg));
  Multiplexer #(.width(32)) multiplexer_6 (
    .in0(multiplexer_4_out), .in1(splitjumpaddress_1_addressjump), .out(multiplexer_6_out), .sel(Jump));
  SplitJumpAddress splitjumpaddress_1 (
    .Address(Address), .PCPlus4(PCPlus4), .AddressJump(splitjumpaddress_1_addressjump));
  DataMem datamem_1 (
    .Reset(Reset), .MemWrite(MemWrite), .Address(alu_1_aluresult), .WriteData(WriteMData),
    .MeamRead(MemRead), .CLK(CLK), .ReadData(datamem_1_readdata));
  Multiplexer #(.width(32)) multiplexer_7 (
    .in0(alu_1_aluresult), .in1(datamem_1_readdata), .out(multiplexer_7_out), .sel(MemToRead));
  Multiplexer #(.width(32)) multiplexer_8 (.in0(multiplexer_7_out), .in1(PCPlus4), .out(WriteData), .sel(Link));
endmodule

module IFetch (
  input  [31:0] nextPC,
  input  CLK,
  input  Reset,
  output [31:0] PCplus4,
  output [31:0] Instruction
);

  wire [1:0] register_1_q, register_1_q_2, register_1_q_3, register_1_q_4, register_1_q_5, register_1_q_6,
       register_1_q_7, register_1_q_8, register_1_q_9, register_1_q_10, register_1_q_11, register_1_q_12,
       register_1_q_13, register_1_q_14, register_1_q_15, register_1_q_16;

  Register #(.width(32)) register_1 (
    .D(nextPC), .clk(CLK),
    .Q({register_1_q_8, register_1_q_7, register_1_q_6, register_1_q_5, register_1_q_4, register_1_q_3, register_1_q_2, register_1_q_16, register_1_q_15, register_1_q_14, register_1_q_13, register_1_q_12, register_1_q_11, register_1_q_10, register_1_q_9, register_1_q}),
    .clr(Reset));  // open: en
  Adder #(.width(32)) adder_1 (
    .a(32'h4),
    .b({register_1_q_8, register_1_q_7, register_1_q_6, register_1_q_5, register_1_q_4, register_1_q_3, register_1_q_2, register_1_q_16, register_1_q_15, register_1_q_14, register_1_q_13, register_1_q_12, register_1_q_11, register_1_q_10, register_1_q_9, register_1_q}),
    .out(PCplus4));  // open: cin, cout
  ROM #(.addrWidth(16), .dataWidth(32)) rom_1 (
    .addr({register_1_q_16, register_1_q_15, register_1_q_14, register_1_q_13, register_1_q_12, register_1_q_11, register_1_q_10, register_1_q_9}),
    .data(Instruction));

  // Notes on the sheet:
  //   contents of rom_1 (hex, n*v repeats v):
  //   1027 c100003 1027 1024 3e00008
endmodule

module ISplit (
  input  [31:0] Instruction,
  output [5:0] opcode,
  output [15:0] immediate,
  output [25:0] address,
  output [5:0] funct,
  output [4:0] shamt,
  output [4:0] rd,
  output [4:0] rt,
  output [4:0] rs
);


  assign address = Instruction[25:0];
  assign funct = Instruction[5:0];
  assign immediate = Instruction[15:0];
  assign opcode = Instruction[31:26];
  assign rd = Instruction[15:11];
  assign rs = Instruction[25:21];
  assign rt = Instruction[20:16];
  assign shamt = Instruction[10:6];
endmodule

module RegFile (
  input  RegWrite,
  input  [4:0] ReadReg1,
  input  [4:0] ReadReg2,
  input  [4:0] WriteRegister,
  input  [31:0] WriteData,
  input  CLK,
  input  Reset,
  output [31:0] ReadData1,
  output [31:0] out_9
);

  wire decoder_1_out0, decoder_1_out1, decoder_1_out2, decoder_1_out3, decoder_1_out4, decoder_1_out5,
       decoder_1_out6, decoder_1_out7, decoder_1_out8, decoder_1_out9, decoder_1_out10, decoder_1_out11,
       decoder_1_out12, decoder_1_out13, decoder_1_out14, decoder_1_out15, decoder_1_out16, decoder_1_out17,
       decoder_1_out18, decoder_1_out19, decoder_1_out20, decoder_1_out21, decoder_1_out22, decoder_1_out23,
       decoder_1_out24, decoder_1_out25, decoder_1_out26, decoder_1_out27, decoder_1_out28, decoder_1_out29,
       decoder_1_out30, decoder_1_out31;
  wire [31:0] a0, a1, a2, a3, at, fp, gp, k0, k1, ra, s0, s1, s2, s3, s4, s5, s6, s7, sp, t0, t1, t2, t3, t4,
       t5, t6, t7, t8, t9, v0, v1, zero;

  Register #(.width(32)) u_a0 (.D(WriteData), .en(decoder_1_out4), .clk(CLK), .Q(a0), .clr(Reset));
  Register #(.width(32)) u_v1 (.D(WriteData), .en(decoder_1_out3), .clk(CLK), .Q(v1), .clr(Reset));
  Register #(.width(32)) u_v0 (.D(WriteData), .en(decoder_1_out2), .clk(CLK), .Q(v0), .clr(Reset));
  Register #(.width(32)) u_at (.D(WriteData), .en(decoder_1_out1), .clk(CLK), .Q(at), .clr(Reset));
  Register #(.width(32)) u_zero (.D(WriteData), .en(decoder_1_out0), .clk(CLK), .Q(zero), .clr(Reset));
  Register #(.width(32)) u_t1 (.D(WriteData), .en(decoder_1_out9), .clk(CLK), .Q(t1), .clr(Reset));
  Register #(.width(32)) u_t0 (.D(WriteData), .en(decoder_1_out8), .clk(CLK), .Q(t0), .clr(Reset));
  Register #(.width(32)) u_a3 (.D(WriteData), .en(decoder_1_out7), .clk(CLK), .Q(a3), .clr(Reset));
  Register #(.width(32)) u_a2 (.D(WriteData), .en(decoder_1_out6), .clk(CLK), .Q(a2), .clr(Reset));
  Register #(.width(32)) u_a1 (.D(WriteData), .en(decoder_1_out5), .clk(CLK), .Q(a1), .clr(Reset));
  Decoder #(.select(5)) decoder_1 (
    .out0(decoder_1_out0), .out1(decoder_1_out1), .out2(decoder_1_out2), .out3(decoder_1_out3),
    .out4(decoder_1_out4), .out5(decoder_1_out5), .out6(decoder_1_out6), .out7(decoder_1_out7),
    .out8(decoder_1_out8), .out9(decoder_1_out9), .out10(decoder_1_out10), .out11(decoder_1_out11),
    .out12(decoder_1_out12), .out13(decoder_1_out13), .out14(decoder_1_out14), .out15(decoder_1_out15),
    .out16(decoder_1_out16), .out17(decoder_1_out17), .out18(decoder_1_out18), .out19(decoder_1_out19),
    .out20(decoder_1_out20), .out21(decoder_1_out21), .out22(decoder_1_out22), .out23(decoder_1_out23),
    .out24(decoder_1_out24), .out25(decoder_1_out25), .out26(decoder_1_out26), .out27(decoder_1_out27),
    .out28(decoder_1_out28), .out29(decoder_1_out29), .out30(decoder_1_out30), .out31(decoder_1_out31),
    .sel(WriteRegister), .en(RegWrite));
  Register #(.width(32)) u_t6 (.D(WriteData), .en(decoder_1_out14), .clk(CLK), .Q(t6), .clr(Reset));
  Register #(.width(32)) u_t5 (.D(WriteData), .en(decoder_1_out13), .clk(CLK), .Q(t5), .clr(Reset));
  Register #(.width(32)) u_t4 (.D(WriteData), .en(decoder_1_out12), .clk(CLK), .Q(t4), .clr(Reset));
  Register #(.width(32)) u_t3 (.D(WriteData), .en(decoder_1_out11), .clk(CLK), .Q(t3), .clr(Reset));
  Register #(.width(32)) u_t2 (.D(WriteData), .en(decoder_1_out10), .clk(CLK), .Q(t2), .clr(Reset));
  Register #(.width(32)) u_s3 (.D(WriteData), .en(decoder_1_out19), .clk(CLK), .Q(s3), .clr(Reset));
  Register #(.width(32)) u_s2 (.D(WriteData), .en(decoder_1_out18), .clk(CLK), .Q(s2), .clr(Reset));
  Register #(.width(32)) u_s1 (.D(WriteData), .en(decoder_1_out17), .clk(CLK), .Q(s1), .clr(Reset));
  Register #(.width(32)) u_s0 (.D(WriteData), .en(decoder_1_out16), .clk(CLK), .Q(s0), .clr(Reset));
  Register #(.width(32)) u_t7 (.D(WriteData), .en(decoder_1_out15), .clk(CLK), .Q(t7), .clr(Reset));
  Register #(.width(32)) u_t8 (.D(WriteData), .en(decoder_1_out24), .clk(CLK), .Q(t8), .clr(Reset));
  Register #(.width(32)) u_s7 (.D(WriteData), .en(decoder_1_out23), .clk(CLK), .Q(s7), .clr(Reset));
  Register #(.width(32)) u_s6 (.D(WriteData), .en(decoder_1_out22), .clk(CLK), .Q(s6), .clr(Reset));
  Register #(.width(32)) u_s5 (.D(WriteData), .en(decoder_1_out21), .clk(CLK), .Q(s5), .clr(Reset));
  Register #(.width(32)) u_s4 (.D(WriteData), .en(decoder_1_out20), .clk(CLK), .Q(s4), .clr(Reset));
  Register #(.width(32)) u_sp (.D(WriteData), .en(decoder_1_out29), .clk(CLK), .Q(sp), .clr(Reset));
  Register #(.width(32)) u_gp (.D(WriteData), .en(decoder_1_out28), .clk(CLK), .Q(gp), .clr(Reset));
  Register #(.width(32)) u_k1 (.D(WriteData), .en(decoder_1_out27), .clk(CLK), .Q(k1), .clr(Reset));
  Register #(.width(32)) u_k0 (.D(WriteData), .en(decoder_1_out26), .clk(CLK), .Q(k0), .clr(Reset));
  Register #(.width(32)) u_t9 (.D(WriteData), .en(decoder_1_out25), .clk(CLK), .Q(t9), .clr(Reset));
  Register #(.width(32)) u_ra (.D(WriteData), .en(decoder_1_out31), .clk(CLK), .Q(ra), .clr(Reset));
  Register #(.width(32)) u_fp (.D(WriteData), .en(decoder_1_out30), .clk(CLK), .Q(fp), .clr(Reset));
  Multiplexer #(.select(5), .width(32)) multiplexer_1 (
    .in0(zero), .in1(at), .in2(v0), .in3(v1), .in4(a0), .in5(a1), .in6(a2), .in7(a3), .in8(t0), .in9(t1),
    .in10(t2), .in11(t3), .in12(t4), .in13(t5), .in14(t6), .in15(t7), .in16(s0), .in17(s1), .in18(s2),
    .in19(s3), .in20(s4), .in21(s5), .in22(s6), .in23(s7), .in24(t8), .in25(t9), .in26(k0), .in27(k1),
    .in28(gp), .in29(sp), .in30(fp), .in31(ra), .out(ReadData1), .sel(ReadReg1));
  Multiplexer #(.select(5), .width(32)) multiplexer_2 (
    .in0(zero), .in1(at), .in2(v0), .in3(v1), .in4(a0), .in5(a1), .in6(a2), .in7(a3), .in8(t0), .in9(t1),
    .in10(t2), .in11(t3), .in12(t4), .in13(t5), .in14(t6), .in15(t7), .in16(s0), .in17(s1), .in18(s2),
    .in19(s3), .in20(s4), .in21(s5), .in22(s6), .in23(s7), .in24(t8), .in25(t9), .in26(k0), .in27(k1),
    .in28(gp), .in29(sp), .in30(fp), .in31(ra), .out(out_9), .sel(ReadReg2));

  // Other names for the same wires on the sheet: rr1[4:0] = ReadReg1; rr2[4:0] = ReadReg2; wd[31:0] = WriteData
endmodule

module ALU (
  input  [31:0] A,
  input  [31:0] B,
  input  [2:0] ALUOperation,
  output zero,
  output [31:0] ALUResult
);

  wire [0:0] SLT;
  wire [31:0] ADD, LAND, LNOR, LOR, SUB;

  Adder #(.width(32)) adder_1 (.a(A), .b(B), .out(ADD));  // open: cin, cout
  Subtractor #(.width(32)) subtractor_1 (.a(A), .b(B), .out(SUB));  // open: bin, bout
  assign LAND = A & B;  // AND_Gate and_1, 32 bits wide
  assign LOR = A | B;  // OR_Gate or_1, 32 bits wide
  assign LNOR = ~LOR;  // NOT_Gate not_1, 32 bits wide
  Comparator #(.width(32)) comparator_1 (.a(A), .b(B), .lt(SLT[0]));  // open: gt, eq
  Multiplexer #(.select(3), .width(32)) multiplexer_1 (
    .in0(SUB), .in1(ADD), .in2({{31{1'b0}}, SLT[0]}), .in3({32{1'b0}}), .in4(LAND), .in5(LNOR), .in6(LOR),
    .in7({32{1'b0}}), .out(ALUResult), .sel(ALUOperation));
  Comparator #(.width(32)) comparator_2 (.a({32{1'b0}}), .b(ALUResult), .eq(zero));  // open: gt, lt
endmodule

module DataMem (
  input  Reset,
  input  MemWrite,
  input  [31:0] Address,
  input  [31:0] WriteData,
  input  MeamRead,
  input  CLK,
  output [31:0] ReadData
);

  RAM #(.asyncread("true"), .clearpin("true"), .dataWidth(32)) ram_1 (
    .addr(Address[9:2]), .we(MemWrite), .oe(MeamRead), .clk(CLK), .din(WriteData), .dout(ReadData),
    .clr(Reset));
endmodule

module LogicControl (
  input  Op5,
  input  Op4,
  input  Op3,
  input  Op2,
  input  Op1,
  input  Op0,
  output RegDst,
  output Jump,
  output Branch,
  output MemRead,
  output MemToReg,
  output [1:0] ALUop,
  output MemWrite,
  output ALUSrc,
  output RegWrite,
  output Link
);

  wire and_1_out, and_2_out, and_3_out, and_4_out, and_5_out, and_6_out, and_7_out, and_8_out, and_9_out,
       and_10_out, and_12_out, and_13_out, and_14_out, and_15_out, and_16_out, and_17_out, not_1_out,
       not_2_out, not_3_out, not_4_out, not_6_out;

  not not_1 (not_1_out, Op5);
  not not_2 (not_2_out, Op4);
  not not_3 (not_3_out, Op3);
  not not_4 (not_4_out, Op2);
  not not_5 (RegDst, Op1);
  not not_6 (not_6_out, Op0);
  and and_1 (and_1_out, RegDst, Op0);
  or or_1 (Jump, and_1_out, and_2_out);
  and and_2 (and_2_out, not_1_out, not_2_out, not_3_out, not_4_out, Op1);
  and and_3 (and_3_out, Op5, not_3_out, Op1);
  and and_4 (and_4_out, not_3_out, Op2, Op1);
  or or_2 (MemRead, and_3_out, and_4_out, and_5_out);
  and and_5 (and_5_out, Op4, not_3_out, Op1);
  and and_6 (and_6_out, RegDst, Op0);
  and and_7 (and_7_out, Op2, Op0);
  and and_8 (and_8_out, Op3, Op0);
  and and_9 (and_9_out, Op4, Op0);
  and and_10 (and_10_out, Op5, Op0);
  and and_11 (ALUop[1], not_4_out, RegDst);
  and and_12 (and_12_out, not_4_out, RegDst, not_6_out);
  and and_13 (and_13_out, not_3_out, Op1, Op0);
  and and_14 (and_14_out, not_3_out, Op2, Op1);
  and and_15 (and_15_out, Op3, not_4_out, not_6_out);
  and and_16 (and_16_out, Op4, not_4_out, not_6_out);
  and and_17 (and_17_out, Op5, not_4_out, not_6_out);
  and and_18 (Link, not_1_out, not_2_out, not_3_out, not_4_out, Op1, Op0);
  or or_3 (MemToReg, and_6_out, and_7_out, and_8_out, and_9_out, and_10_out);
  or or_4 (RegWrite, and_12_out, and_13_out, and_14_out, and_15_out, and_16_out, and_17_out);

  assign ALUop[0] = Op2;
  assign ALUSrc = Op0;
  assign Branch = Op2;
  assign MemWrite = Op3;
endmodule

module Control (
  input  [5:0] OpCode,
  output RegDst,
  output Jump,
  output Branch,
  output MemRead,
  output MemToReg,
  output [1:0] ALUOp,
  output MemWrite,
  output ALUSrc,
  output RegWrite,
  output Link
);

  LogicControl logiccontrol_1 (
    .Op5(OpCode[5]), .Op4(OpCode[4]), .Op3(OpCode[3]), .Op2(OpCode[2]), .Op1(OpCode[1]), .Op0(OpCode[0]),
    .RegDst(RegDst), .Jump(Jump), .Branch(Branch), .MemRead(MemRead), .MemToReg(MemToReg), .ALUop(ALUOp),
    .MemWrite(MemWrite), .ALUSrc(ALUSrc), .RegWrite(RegWrite), .Link(Link));
endmodule

module ALUControl (
  input  [1:0] ALUOpIn,
  input  [5:0] Instruction,
  output [2:0] ALUOpOut,
  output JumpReg
);

  wire and_2_out, and_3_out, and_4_out, and_5_out, and_6_out, and_7_out, and_8_out, and_9_out, and_10_out,
       not_1_out, not_2_out, not_3_out, not_4_out, not_5_out, not_6_out, not_7_out, not_8_out;

  not not_1 (not_1_out, ALUOpIn[1]);
  not not_2 (not_2_out, ALUOpIn[0]);
  not not_3 (not_3_out, Instruction[5]);
  not not_4 (not_4_out, Instruction[4]);
  not not_5 (not_5_out, Instruction[3]);
  not not_6 (not_6_out, Instruction[2]);
  not not_7 (not_7_out, Instruction[1]);
  not not_8 (not_8_out, Instruction[0]);
  and and_1 (ALUOpOut[2], ALUOpIn[1], Instruction[2]);
  and and_2 (and_2_out, ALUOpIn[1], not_3_out, not_5_out, Instruction[0]);
  and and_3 (and_3_out, ALUOpIn[1], Instruction[3], not_6_out);
  and and_4 (and_4_out, ALUOpIn[1], not_6_out, Instruction[0]);
  and and_5 (and_5_out, ALUOpIn[1], not_5_out, not_7_out, Instruction[0]);
  and and_6 (and_6_out, ALUOpIn[1], Instruction[4], not_5_out, Instruction[0]);
  and and_7 (and_7_out, ALUOpIn[1], ALUOpIn[0], not_5_out, Instruction[0]);
  and and_8 (and_8_out, not_1_out, not_2_out);
  and and_9 (and_9_out, not_2_out, not_6_out, not_7_out);
  and and_10 (and_10_out, ALUOpIn[1], Instruction[1], Instruction[0]);
  and and_11 (JumpReg, ALUOpIn[1], not_2_out, not_3_out, not_4_out, Instruction[3], not_6_out, not_7_out, not_8_out);
  or or_1 (ALUOpOut[1], and_2_out, and_3_out, and_4_out, and_5_out, and_6_out, and_7_out);
  or or_2 (ALUOpOut[0], and_8_out, and_9_out, and_10_out);
endmodule

module Extend16 (
  input  [15:0] in_1,
  output [31:0] out_2
);


  assign out_2 = {{16{1'b0}}, in_1};
endmodule

module SplitJumpAddress (
  input  [25:0] Address,
  input  [31:0] PCPlus4,
  output [31:0] AddressJump
);


  assign AddressJump = {PCPlus4[29:28], PCPlus4[31:30], Address, 2'b00};
endmodule
